# Fritzing sketch CarteDomeESP32_Circuit (saved by Fritzing 0.9.3b)
stripboards: 1

parts:
  U3 = ESP32S-HiLetgo [part_number=ESP32S-HiLetgo]
  IC2 = MCP23017 I2C I/O Expander
  Composant2 = Logic Level Converter
  0V_12V = KF301-2 [part_number=KF301-2 package="screwterminal-5mm 2 position"]
  5V = KF301-2 [part_number=KF301-2 package="screwterminal-5mm 2 position"]
  Capteurs_GND/12V = KF301-2 [part_number=KF301-2 package="screwterminal-5mm 2 position"]
  Abri = KF301-2 [part_number=KF301-2 package="screwterminal-5mm 2 position"]
  Porte_1 = KF301-2 [part_number=KF301-2 package="screwterminal-5mm 2 position"]
  Porte_2 = KF301-2 [part_number=KF301-2 package="screwterminal-5mm 2 position"]
  Boutons_+_GND = male pin header, 5 pins [form="♂ (male)"]
  TM1638 = male pin header, 5 pins [form="♂ (male)"]
  i2c = male pin header, 4 pins [form="♂ (male)"]
  i2c1 = male pin header, 4 pins [form="♂ (male)"]
  i2c2 = male pin header, 4 pins [form="♂ (male)"]
  i2c3 = male pin header, 4 pins [form="♂ (male)"]
  Lcd = male pin header, 2 pins [form="♂ (male)"]
  APA106 = male pin header, 3 pins [form="♂ (male)"]
  i2c4 = male pin header, 4 pins [form="♂ (male)"]
  U6 = V_REG_LD1117VXX [package=78xxl]
  R1 = Resistor [tolerance=±5% resistance=100 package="0603 [SMD]"]
  Park = male alternating pin header, 2 pins [form="♂ (male)"]

nets:
  N1: U3.3.3, U3.GND, IC2.SCL, Composant2.RX2_HV, i2c.pin3, i2c1.pin3, i2c2.pin3, i2c3.pin3, i2c4.pin3
  N2: U3.EN, Composant2.TX2_LV, 5V.1
  N3: U3.GPIO36, Composant2.TX_LV
  N4: U3.GPIO33, TM1638.pin3
  N5: U3.GPIO25, R1.Pin_0
  N6: U3.GPIO9, Composant2.RX_LV
  N7: U3.GPIO10, U3.GPIO8, Composant2.LV
  N8: U3.GPIO11, U3.GPIO7, IC2.VDD, IC2.RESET, Composant2.HV, 5V.2, i2c.pin1, i2c1.pin1, i2c2.pin1, i2c3.pin1, APA106.pin2, i2c4.pin1, U6.IN
  GND: U3.VIN, U3.GPIO6, IC2.VSS, IC2.A0, IC2.A1, IC2.A2, Composant2.GND, 0V_12V.2, Capteurs_GND/12V.1, Boutons_+_GND.pin5, TM1638.pin4, i2c.pin2, i2c1.pin2, i2c2.pin2, i2c3.pin2, Lcd.pin1, APA106.pin1, i2c4.pin2, U6.GND, Park.pin2
  N9: U3.GPIO17, Composant2.RX2_LV
  N10: U3.GPIO18, Lcd.pin2
  N11: U3.GPIO1, TM1638.pin1
  N12: U3.GPIO22, TM1638.pin2
  N13: IC2.GPB0, Boutons_+_GND.pin4
  N14: IC2.GPB1, Boutons_+_GND.pin3
  N15: IC2.GPB2, Boutons_+_GND.pin2
  N16: IC2.GPB3, Boutons_+_GND.pin1
  N17: IC2.SDA, Composant2.TX2_HV, i2c.pin4, i2c1.pin4, i2c2.pin4, i2c3.pin4, i2c4.pin4
  N18: IC2.GPA0, Porte_2.2
  N19: IC2.GPA2, Porte_2.1
  N20: IC2.GPA4, Porte_1.2
  N21: IC2.GPA5, Abri.2
  N22: IC2.GPA6, Porte_1.1
  N23: IC2.GPA7, Abri.1
  N24: Composant2.TX_HV, APA106.pin3
  N25: 0V_12V.1, Capteurs_GND/12V.2
  N26: TM1638.pin5, U6.OUT
  N27: R1.Pin_1, Park.pin1

custom parts:
  ESP32S-HiLetgo: HiLetgo ESP-WROOM-32 ESP32 ESP-32S Development Board 2.4GHz Dual-Mode WiFi + Bluetooth Dual Cores Microcontroller The ESP32 integrated with Antenna switches, RF Balun, power amplifiers, low-noise amplifiers, filters, and management modules, and the entire solution occupies the least area of PCB. 2.4 GHz Wi-Fi plus Bluetooth dual-mode chip, with TSMC Ultra-low power consumption 40nm technology,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
  MCP23017 I2C I/O Expander: The MCP23017 uses two i2c pins (these can be shared with other i2c devices), and in exchange gives you 16 general purpose pins. You can set each of 16 pins to be input, output, input with a pullup or open drain. There's even the ability to get an interrupt via an external pin when any of the inputs change so you don't have to keep polling the chip.
  KF301-2: KF301-3 is a 3 position screw terminal header block with male through hole PCB pins on 5mm spacing
