# Fritzing sketch CarteDomeNano_CircuitV2 (saved by Fritzing 0.9.3b)
stripboards: 1

parts:
  0V_12V = KF301-2 [part_number=KF301-2 package="screwterminal-5mm 2 position"]
  5V = KF301-2 [part_number=KF301-2 package="screwterminal-5mm 2 position"]
  Capteurs_GND/12V = KF301-2 [part_number=KF301-2 package="screwterminal-5mm 2 position"]
  Abri = KF301-2 [part_number=KF301-2 package="screwterminal-5mm 2 position"]
  Porte_1 = KF301-2 [part_number=KF301-2 package="screwterminal-5mm 2 position"]
  Porte_2 = KF301-2 [part_number=KF301-2 package="screwterminal-5mm 2 position"]
  TM1638 = male pin header, 5 pins [form="♂ (male)"]
  i2c = male pin header, 4 pins [form="♂ (male)"]
  APA106 = male pin header, 3 pins [form="♂ (male)"]
  Composant1 = Arduino Nano (Rev3.0)
  i2c2 = male pin header, 4 pins [form="♂ (male)"]
  i2c3 = male pin header, 4 pins [form="♂ (male)"]
  WeMos_D1_Mini1 = WeMos D1 Mini
  Composant3 = Logic Level Converter
  IC3 = MCP23017 I2C I/O Expander
  Lcd = male pin header, 1 pin [form="♂ (male)"]
  UART = male pin header, 4 pins [form="♂ (male)"]
  Boutons_+_GND = male pin header, 10 pins [form="♂ (male)"]
  R3 = Resistor [tolerance=±5% resistance=4.7k package="0603 [SMD]"]
  R4 = Resistor [tolerance=±5% resistance=4.7k package="0603 [SMD]"]
  Relais+_alim = male pin header, 10 pins [form="♂ (male)"]
  Park/ARU = KF301-2 [part_number=KF301-2 package="screwterminal-5mm 2 position"]
  UART2 = male pin header, 4 pins [form="♂ (male)"]
  UART3 = male pin header, 4 pins [form="♂ (male)"]
  M/A = KF301-2 [part_number=KF301-2 package="screwterminal-5mm 2 position"]
  R5 = Resistor [tolerance=±5% resistance=10k package="0603 [SMD]"]
  R6 = Resistor [tolerance=±5% resistance=10k package="0603 [SMD]"]

nets:
  N1: 0V_12V.1, Capteurs_GND/12V.2
  GND: 0V_12V.2, Capteurs_GND/12V.1, TM1638.pin2, i2c.pin3, APA106.pin3, Composant1.GND, i2c2.pin3, i2c3.pin3, WeMos_D1_Mini1.G, Composant3.GND, IC3.VSS, IC3.A0, IC3.A1, IC3.A2, UART.pin4, Boutons_+_GND.pin10, Relais+_alim.pin1, UART2.pin2, UART3.pin2, M/A.2, R6.Pin_0
  5V: 5V.2, TM1638.pin1, i2c.pin4, APA106.pin2, Composant1.5V, i2c2.pin4, i2c3.pin4, WeMos_D1_Mini1.5V, Composant3.HV, IC3.VDD, IC3.RESET, Boutons_+_GND.pin1, R3.Pin_0, R4.Pin_0, Relais+_alim.pin10, UART3.pin1, R5.Pin_1
  N2: Abri.1, IC3.GPA7
  N3: Abri.2, IC3.GPA5
  N4: Porte_1.1, IC3.GPA6
  N5: Porte_1.2, IC3.GPA4
  N6: Porte_2.1, IC3.GPA2
  N7: Porte_2.2, IC3.GPA0
  N8: TM1638.pin3, Composant1.A0
  N9: TM1638.pin4, Composant1.A1
  N10: TM1638.pin5, Composant1.A2
  N11: i2c.pin1, Composant1.A4, i2c2.pin1, i2c3.pin1, IC3.SDA, R4.Pin_1
  N12: i2c.pin2, Composant1.A5, i2c2.pin2, i2c3.pin2, IC3.SCL, R3.Pin_1
  N13: APA106.pin1, Composant1.D4
  N14: Composant1.D1/TX, Composant3.TX_HV
  N15: Composant1.D0/RX, Composant3.RX_HV
  N16: Composant1.RESET, WeMos_D1_Mini1.D6
  N17: Composant1.D2, Composant3.TX2_HV, UART3.pin4
  N18: Composant1.D3, Lcd.pin1
  N19: Composant1.D5, Relais+_alim.pin9
  N20: Composant1.D6, Relais+_alim.pin8
  N21: Composant1.D7, Relais+_alim.pin7
  N22: Composant1.D8, Relais+_alim.pin6
  N23: Composant1.D9, Relais+_alim.pin5
  N24: Composant1.D10, Relais+_alim.pin4
  N25: Composant1.D11/MOSI, Relais+_alim.pin3
  N26: Composant1.D12/MISO, Relais+_alim.pin2
  N27: Composant1.A6, M/A.1, R5.Pin_0
  N28: Composant1.3V3, Composant3.LV, UART.pin3, UART2.pin1
  N29: Composant1.D13/SCK, Composant3.RX2_HV, UART3.pin3
  N30: WeMos_D1_Mini1.RX, Composant3.TX_LV, UART.pin1
  N31: WeMos_D1_Mini1.TX, Composant3.RX_LV, UART.pin2
  N32: Composant3.TX2_LV, UART2.pin4
  N33: Composant3.RX2_LV, UART2.pin3
  N34: IC3.GPB0, Boutons_+_GND.pin9
  N35: IC3.GPB1, Boutons_+_GND.pin8
  N36: IC3.GPB2, Boutons_+_GND.pin7
  N37: IC3.GPB3, Boutons_+_GND.pin6
  N38: IC3.GPB4, Boutons_+_GND.pin5
  N39: IC3.GPB5, Boutons_+_GND.pin4
  N40: IC3.GPB6, Boutons_+_GND.pin3
  N41: IC3.GPB7, Boutons_+_GND.pin2
  N42: IC3.GPA1, Park/ARU.1, R6.Pin_1
  N43: IC3.GPA3, Park/ARU.2

custom parts:
  KF301-2: KF301-3 is a 3 position screw terminal header block with male through hole PCB pins on 5mm spacing
  WeMos D1 Mini: The D1 mini is a mini wifi board based on ESP-8266EX.
  MCP23017 I2C I/O Expander: The MCP23017 uses two i2c pins (these can be shared with other i2c devices), and in exchange gives you 16 general purpose pins. You can set each of 16 pins to be input, output, input with a pullup or open drain. There's even the ability to get an interrupt via an external pin when any of the inputs change so you don't have to keep polling the chip.
