# Fritzing sketch DomeMega (saved by Fritzing 0.9.3b)
stripboards: 1

parts:
  i2c5 = male pin header, 4 pins [form="♂ (male)"]
  i2c6 = male pin header, 4 pins [form="♂ (male)"]
  i2c7 = male pin header, 4 pins [form="♂ (male)"]
  TM1638 = male pin header, 5 pins [form="♂ (male)"]
  Composant3 = Logic Level Converter
  Nano_E/S = male pin header, 4 pins [form="♂ (male)"]  # not connected
  i2c9 = male pin header, 4 pins [form="♂ (male)"]
  APA106 = male pin header, 3 pins [form="♂ (male)"]  # not connected
  Serial_ESP32 = male pin header, 3 pins [form="♂ (male)"]
  BackLight = male pin header, 1 pin [form="♂ (male)"]
  Composant4 = Arduino Mega 2560 (Rev3)  # not connected

nets:
  N1: i2c5.pin1, i2c6.pin1, i2c7.pin1, TM1638.pin3, i2c9.pin1
  N2: i2c5.pin2, i2c6.pin2, i2c7.pin2, TM1638.pin4, i2c9.pin2
  N3: i2c5.pin3, i2c6.pin3, i2c7.pin3, TM1638.pin5, i2c9.pin3
  N4: i2c5.pin4, i2c6.pin4, i2c7.pin4, i2c9.pin4
  N5: Composant3.TX2_LV, Composant3.TX2_HV, Serial_ESP32.pin3
  N6: Composant3.RX2_LV, Composant3.RX2_HV, Serial_ESP32.pin2
  N7: Composant3.GND, Serial_ESP32.pin1
  N8: Composant3.LV, Composant3.HV, BackLight.pin1
  N9: Composant3.RX_LV, Composant3.RX_HV
  N10: Composant3.TX_LV, Composant3.TX_HV
