# Fritzing sketch NanoIHM (saved by Fritzing 0.9.3b)
stripboards: 1

parts:
  i2c5 = male pin header, 4 pins [form="♂ (male)"]
  i2c6 = male pin header, 4 pins [form="♂ (male)"]
  i2c7 = male pin header, 4 pins [form="♂ (male)"]
  TM1638 = male pin header, 5 pins [form="♂ (male)"]
  Composant3 = Logic Level Converter
  Composant4 = Arduino Nano (Rev3.0)
  Nano_E/S = male pin header, 4 pins [form="♂ (male)"]
  i2c9 = male pin header, 4 pins [form="♂ (male)"]
  APA106 = male pin header, 3 pins [form="♂ (male)"]
  Serial_ESP32 = male pin header, 3 pins [form="♂ (male)"]
  BackLight = male pin header, 1 pin [form="♂ (male)"]

nets:
  N1: i2c5.pin1, i2c6.pin1, i2c7.pin1, Composant4.A4, i2c9.pin1
  N2: i2c5.pin2, i2c6.pin2, i2c7.pin2, Composant4.A5, i2c9.pin2
  GND: i2c5.pin3, i2c6.pin3, i2c7.pin3, TM1638.pin4, Composant3.GND, Composant4.GND, Nano_E/S.pin1, i2c9.pin3, APA106.pin1, Serial_ESP32.pin1
  N3: i2c5.pin4, i2c6.pin4, i2c7.pin4, TM1638.pin5, Composant3.TX_HV, Composant3.HV, Composant4.5V, i2c9.pin4, APA106.pin2
  N4: TM1638.pin1, Composant4.D7
  N5: TM1638.pin2, Composant4.D6
  N6: TM1638.pin3, Composant4.D5
  N7: Composant3.TX2_LV, Serial_ESP32.pin3
  N8: Composant3.RX2_LV, Serial_ESP32.pin2
  N9: Composant3.LV, Composant4.3V3
  N10: Composant3.RX_HV, Composant4.D13/SCK
  N11: Composant3.RX2_HV, Composant4.A0
  N12: Composant3.TX2_HV, Composant4.A1
  N13: Composant4.D1/TX, Nano_E/S.pin4
  N14: Composant4.D0/RX, Nano_E/S.pin3
  N15: Composant4.D3, APA106.pin3
  N16: Composant4.D11/MOSI, BackLight.pin1
